// Logisim project new-main.circ as structural Verilog: 6 circuits, main circuit LOCK
module LOCK (
  input  ON_OFF,
  input  SET_PASSWORD,
  input  INPUT_PASSWORD
);

  wire _0_out, _1_out, _2_out, _3_out, _4_out, _5_out, _6_out, _7_out, _8_out, _9_out, comparator_1_b,
       comparator_1_c, comparator_1_d, comparator_1_e, comparator_1_f, comparator_1_g, comparator_1_g_2,
       comparator_1_out_17, decimal_to_excess_iii_1_out_12, decimal_to_excess_iii_1_out_13,
       decimal_to_excess_iii_1_out_14, decimal_to_excess_iii_1_out_15, decimal_to_excess_iii_1_out_16,
       memory_1_out_15, memory_1_out_16, memory_1_out_17, memory_1_out_18, memory_2_p6, memory_2_p8,
       memory_2_p10, memory_2_p11, memory_2_p12, memory_2_p13, n7_segment_1_a, n7_segment_1_b,
       n7_segment_1_c, n7_segment_1_d, n7_segment_1_dot, n7_segment_1_e, n7_segment_1_f, n7_segment_1_g,
       Retry_out;
  wire [3:0] memory_2_p1;
  wire [7:0] memory_1__1_2, memory_1__1_3, memory_1__2_2, memory_1__13, memory_1__14;

  Button _1 (.out(_1_out));
  Button _2 (.out(_2_out));
  Button _4 (.out(_4_out));
  Button _5 (.out(_5_out));
  Button _7 (.out(_7_out));
  Button _8 (.out(_8_out));
  Button _0 (.out(_0_out));
  Decimal_to_EXCESS_III decimal_to_excess_iii_1 (
    .D0(_0_out), .D1(_1_out), .D2(_2_out), .D3(_3_out), .D4(_4_out), .D5(_5_out), .D6(_6_out), .D7(_7_out),
    .D8(_8_out), .D9(_9_out), .on(ON_OFF), .out_12(decimal_to_excess_iii_1_out_12),
    .out_13(decimal_to_excess_iii_1_out_13), .out_14(decimal_to_excess_iii_1_out_14),
    .out_15(decimal_to_excess_iii_1_out_15), .out_16(decimal_to_excess_iii_1_out_16));
  Button _3 (.out(_3_out));
  Button _6 (.out(_6_out));
  Button _9 (.out(_9_out));
  MEMORY memory_1 (
    .in_2(memory_2_p1), ._1(decimal_to_excess_iii_1_out_12), .out_15(memory_1_out_15),
    .out_16(memory_1_out_16), .out_17(memory_1_out_17), ._2(decimal_to_excess_iii_1_out_13),
    .out_18(memory_1_out_18), ._3(decimal_to_excess_iii_1_out_14), ._4(decimal_to_excess_iii_1_out_15),
    .reser(Retry_out), .enab(INPUT_PASSWORD), .on(1'b1), ._1_3(memory_1__1_3), ._2_2(memory_1__2_2),
    ._13(memory_1__13), ._14(memory_1__14), ._1_2(memory_1__1_2));  // open: in_3
  // MEMORY memory_2: pin names not known; wires that end beside it: memory_2_p1, decimal_to_excess_iii_1_out_12, decimal_to_excess_iii_1_out_13, decimal_to_excess_iii_1_out_14, decimal_to_excess_iii_1_out_15, memory_2_p6, SET_PASSWORD, memory_2_p8, 1'b1, memory_2_p10, memory_2_p11, memory_2_p12, memory_2_p13
  _7_Segment u_7_segment_1 (
    .X3(decimal_to_excess_iii_1_out_12), .X2(decimal_to_excess_iii_1_out_13),
    .X1(decimal_to_excess_iii_1_out_14), .X0(decimal_to_excess_iii_1_out_15),
    .on(decimal_to_excess_iii_1_out_16), .A(n7_segment_1_a), .B(n7_segment_1_b), .C(n7_segment_1_c),
    .D(n7_segment_1_d), .E(n7_segment_1_e), .F(n7_segment_1_f), .G(n7_segment_1_g), .dot(n7_segment_1_dot));
  Button RESET (.out(memory_2_p8));
  Button Retry (.out(Retry_out));
  _7_Segment_Display u_7_segment_display_1 (
    .g(n7_segment_1_g), .f(n7_segment_1_f), .a(n7_segment_1_a), .b(n7_segment_1_b), .e(n7_segment_1_e),
    .d(n7_segment_1_d), .c(n7_segment_1_c), .dp(n7_segment_1_dot));
  Comparator comparator_1 (
    .in_1(memory_2_p10), .in_2(memory_2_p11), .in_3(memory_2_p12), .in_4(memory_2_p13),
    .in_5(memory_1_out_15), .in_6(memory_1_out_16), .in_7(memory_1_out_17), .in_8(memory_1_out_18),
    .in_9(1'b1), .G(comparator_1_g), .B(comparator_1_b), .C(comparator_1_c), .D(comparator_1_d),
    .E(comparator_1_e), .F(comparator_1_f), .G_2(comparator_1_g_2), .out_17(comparator_1_out_17));
  _7_Segment_Display u_7_segment_display_2 (
    .g(comparator_1_g_2), .f(comparator_1_f), .a(comparator_1_g), .b(comparator_1_b), .e(comparator_1_e),
    .d(comparator_1_d), .c(comparator_1_c), .dp(comparator_1_out_17));
  _7_Segment_Display u_7_segment_display_3 (
    .g(memory_1__1_2[6]), .f(memory_1__1_2[5]), .a(memory_1__1_2[0]), .b(memory_1__1_2[1]),
    .e(memory_1__1_2[4]), .d(memory_1__1_2[3]), .c(memory_1__1_2[2]), .dp(memory_1__1_2[7]));
  _7_Segment_Display u_7_segment_display_4 (
    .g(memory_1__14[6]), .f(memory_1__14[5]), .a(memory_1__14[0]), .b(memory_1__14[1]), .e(memory_1__14[4]),
    .d(memory_1__14[3]), .c(memory_1__14[2]), .dp(memory_1__14[7]));
  _7_Segment_Display u_7_segment_display_5 (
    .g(memory_1__13[6]), .f(memory_1__13[5]), .a(memory_1__13[0]), .b(memory_1__13[1]), .e(memory_1__13[4]),
    .d(memory_1__13[3]), .c(memory_1__13[2]), .dp(memory_1__13[7]));
  _7_Segment_Display u_7_segment_display_6 (
    .g(memory_1__2_2[6]), .f(memory_1__2_2[5]), .a(memory_1__2_2[0]), .b(memory_1__2_2[1]),
    .e(memory_1__2_2[4]), .d(memory_1__2_2[3]), .c(memory_1__2_2[2]), .dp(memory_1__2_2[7]));
  _7_Segment_Display u_7_segment_display_7 (
    .g(memory_1__1_3[6]), .f(memory_1__1_3[5]), .a(memory_1__1_3[0]), .b(memory_1__1_3[1]),
    .e(memory_1__1_3[4]), .d(memory_1__1_3[3]), .c(memory_1__1_3[2]), .dp(memory_1__1_3[7]));
endmodule

module Decimal_to_EXCESS_III (
  input  D0,
  input  D1,
  input  D2,
  input  D3,
  input  D4,
  input  D5,
  input  D6,
  input  D7,
  input  D8,
  input  D9,
  input  on,
  output out_12,
  output out_13,
  output out_14,
  output out_15,
  output out_16
);

  wire or_1_out, or_2_out, or_3_out, or_4_out;

  or or_1 (or_1_out, D0, D2, D4, D6, D8);
  or or_2 (or_2_out, D0, D3, D8, D7, D4);
  or or_3 (or_3_out, D2, D3, D9, D4, D1);
  or or_4 (or_4_out, D5, D9, D8, D6, D7);
  and and_1 (out_12, or_1_out, on);
  and and_2 (out_13, or_2_out, on);
  and and_3 (out_14, or_3_out, on);
  and and_4 (out_15, or_4_out, on);
  LED led_1 (.in(out_12));
  LED led_2 (.in(out_13));
  LED led_3 (.in(out_14));
  LED led_4 (.in(out_15));
  or or_5 (out_16, out_12, out_13, out_14, out_15);
  LED led_5 (.in(out_16));
endmodule

// 7 SEG-DECODER
module _7_Segment (
  input  X3,
  input  X2,
  input  X1,
  input  X0,
  input  on,
  output A,
  output B,
  output C,
  output D,
  output E,
  output F,
  output G,
  output dot
);

  wire and_1_out, and_2_out, and_3_out, and_4_out, and_5_out, and_6_out, and_7_out, and_8_out, and_9_out,
       and_10_out, and_11_out, and_12_out, and_13_out, and_14_out, and_15_out, and_16_out, not_1_out,
       not_2_out, not_3_out, not_4_out, not_5_out, not_6_out, not_7_out, not_8_out, not_9_out, not_10_out,
       not_11_out, not_12_out, not_13_out, not_14_out;

  not not_1 (not_1_out, X2);
  and and_1 (and_1_out, not_1_out, X3);
  not not_2 (not_2_out, X1);
  and and_2 (and_2_out, not_2_out, X2);
  and and_3 (and_3_out, X2, not_3_out);
  not not_3 (not_3_out, X3);
  and and_4 (and_4_out, X1, not_4_out);
  not not_4 (not_4_out, X3);
  not not_5 (not_5_out, X1);
  and and_5 (and_5_out, not_5_out, X3);
  not not_6 (not_6_out, X2);
  and and_6 (and_6_out, not_6_out, X3);
  not not_7 (not_7_out, X0);
  and and_7 (and_7_out, not_7_out, X2, not_8_out);
  not not_8 (not_8_out, X3);
  and and_8 (and_8_out, X0, not_9_out);
  not not_9 (not_9_out, X2);
  not not_10 (not_10_out, X1);
  and and_9 (and_9_out, not_10_out, X3);
  not not_11 (not_11_out, X2);
  and and_10 (and_10_out, not_11_out, X3);
  and and_11 (and_11_out, X2, X3);
  and and_12 (and_12_out, X0, not_12_out);
  not not_12 (not_12_out, X2);
  not not_13 (not_13_out, X2);
  and and_13 (and_13_out, not_13_out, X3);
  and and_14 (and_14_out, X1, X2);
  and and_15 (and_15_out, X0, not_14_out);
  not not_14 (not_14_out, X2);
  and and_16 (and_16_out, X0, X3);
  or or_1 (A, and_1_out, and_2_out, and_3_out, X0);
  or or_2 (B, X2, X1);
  or or_3 (C, X2, and_4_out, X0);
  or or_4 (D, and_5_out, and_6_out, and_7_out, and_8_out);
  or or_5 (E, and_9_out, and_10_out);
  or or_6 (F, and_11_out, and_12_out);
  or or_7 (G, and_13_out, and_14_out, and_15_out, and_16_out);

  assign dot = on;
endmodule

// COMPARATOR
module Comparator (
  input  in_1,
  input  in_2,
  input  in_3,
  input  in_4,
  input  in_5,
  input  in_6,
  input  in_7,
  input  in_8,
  input  in_9,
  output G,
  output B,
  output C,
  output D,
  output E,
  output F,
  output G_2,
  output out_17
);

  wire and_1_out, not_1_out, not_2_out, not_3_out, not_4_out, xor_1_out, xor_2_out, xor_3_out, xor_4_out;

  xor xor_1 (xor_1_out, in_1, in_5);
  xor xor_2 (xor_2_out, in_2, in_6);
  xor xor_3 (xor_3_out, in_3, in_7);
  xor xor_4 (xor_4_out, in_4, in_8);
  not not_1 (not_1_out, xor_1_out);
  not not_2 (not_2_out, xor_2_out);
  not not_3 (not_3_out, xor_3_out);
  not not_4 (not_4_out, xor_4_out);
  and and_1 (and_1_out, not_1_out, not_2_out, not_3_out, not_4_out, in_9);
  and and_2 (G, 1'b1, 1'b0);
  and and_3 (B, in_9, and_1_out);
  and and_4 (C, and_1_out, in_9);
  and and_5 (D, 1'b1, in_9);

  assign E = D;
  assign F = D;
  assign G_2 = 1'b0;
  assign out_17 = in_9;
endmodule

// DECODER
module Decoder (
  input  X,
  input  in_2,
  output A,
  output B,
  output C,
  output D,
  output E,
  output F,
  output G,
  output out_10
);

  and and_1 (A, 1'b1, 1'b0);
  and and_2 (B, in_2, X);
  and and_3 (C, X, in_2);
  and and_4 (D, 1'b1, in_2);

  assign E = D;
  assign F = D;
  assign G = 1'b0;
  assign out_10 = in_2;
endmodule

module MEMORY (
  input  reser,
  input  [3:0] in_2,
  input  [3:0] in_3,
  input  _1,
  input  _2,
  input  _3,
  input  _4,
  input  enab,
  input  on,
  output [7:0] _14,
  output [7:0] _2_2,
  output [7:0] _13,
  output [7:0] _1_2,
  output [7:0] _1_3,
  output out_15,
  output out_16,
  output out_17,
  output out_18
);

  wire and_1_out, and_2_out, comparator_1_gt, multiplexer_5_out, multiplexer_6_out, nor_1_out, or_1_out,
       undriven;
  wire [3:0] bit_extender_1_out, counter_1_q, multiplexer_1_out, register_1_q, register_2_q, register_3_q,
       register_4_q;

  Multiplexer multiplexer_1 (.in0(out_15), .in1(_1), .out(multiplexer_1_out[0]), .sel(and_1_out));  // open: en
  Multiplexer multiplexer_2 (.in0(out_16), .in1(_2), .out(multiplexer_1_out[1]), .sel(and_1_out));  // open: en
  Multiplexer multiplexer_3 (.in0(out_17), .in1(_3), .out(multiplexer_1_out[2]), .sel(and_1_out));  // open: en
  Multiplexer multiplexer_4 (.in0(out_18), .in1(_4), .out(multiplexer_1_out[3]), .sel(and_1_out));  // open: en
  and and_1 (and_1_out, nor_1_out, on);
  Multiplexer multiplexer_5 (.in0(or_1_out), .in1(or_1_out), .out(multiplexer_5_out), .sel(or_1_out));  // open: en
  or or_1 (or_1_out, multiplexer_1_out[0], multiplexer_1_out[1], multiplexer_1_out[2], multiplexer_1_out[3]);
  Counter #(.width(4), .max('h6), .ongoal("continue")) counter_1 (
    .D(in_2), .count(1'b1), .Q(counter_1_q), .clk(multiplexer_5_out), .clr(multiplexer_6_out));  // open: load, carry
  Bit_Extender #(.in_width(4), .out_width(4)) bit_extender_1 (.in(multiplexer_1_out), .out(bit_extender_1_out));
  Register #(.width(4)) register_1 (
    .D(bit_extender_1_out), .en(enab), .Q(register_1_q), .clk(multiplexer_5_out), .clr(multiplexer_6_out));
  _7_Segment u_7_segment_1 (
    .X3(register_1_q[0]), .X2(register_1_q[1]), .X1(register_1_q[2]), .X0(register_1_q[3]), .on(1'b1),
    .A(_1_3[0]), .B(_1_3[1]), .C(_1_3[2]), .D(_1_3[3]), .E(_1_3[4]), .F(_1_3[5]), .G(_1_3[6]), .dot(_1_3[7]));
  Comparator_part #(.width(4)) comparator_1 (.a(in_3), .b(counter_1_q), .gt(comparator_1_gt));  // open: eq, lt
  Register #(.width(4)) register_2 (
    .D(register_1_q), .en(enab), .Q(register_2_q), .clk(multiplexer_5_out), .clr(multiplexer_6_out));
  _7_Segment u_7_segment_2 (
    .X3(register_2_q[0]), .X2(register_2_q[1]), .X1(register_2_q[2]), .X0(register_2_q[3]), .on(1'b1),
    .A(_2_2[0]), .B(_2_2[1]), .C(_2_2[2]), .D(_2_2[3]), .E(_2_2[4]), .F(_2_2[5]), .G(_2_2[6]), .dot(_2_2[7]));
  Register #(.width(4)) register_3 (
    .D(register_2_q), .en(enab), .Q(register_3_q), .clk(multiplexer_5_out), .clr(multiplexer_6_out));
  _7_Segment u_7_segment_3 (
    .X3(register_3_q[0]), .X2(register_3_q[1]), .X1(register_3_q[2]), .X0(register_3_q[3]), .on(1'b1),
    .A(_13[0]), .B(_13[1]), .C(_13[2]), .D(_13[3]), .E(_13[4]), .F(_13[5]), .G(_13[6]), .dot(_13[7]));
  Multiplexer multiplexer_6 (.in0(and_2_out), .in1(reser), .out(multiplexer_6_out), .sel(reser), .en(undriven));
  Register #(.width(4)) register_4 (
    .D(register_3_q), .en(enab), .Q(register_4_q), .clk(multiplexer_5_out), .clr(multiplexer_6_out));
  nor nor_1 (nor_1_out, out_15, out_16, out_17, out_18);
  _7_Segment u_7_segment_4 (
    .X3(register_4_q[0]), .X2(register_4_q[1]), .X1(register_4_q[2]), .X0(register_4_q[3]), .on(1'b1),
    .A(_14[0]), .B(_14[1]), .C(_14[2]), .D(_14[3]), .E(_14[4]), .F(_14[5]), .G(_14[6]), .dot(_14[7]));
  and and_2 (and_2_out, 1'b1, 1'b0, comparator_1_gt);
  Register #(.width(4)) register_5 (
    .D(register_4_q), .en(enab), .Q({out_18, out_17, out_16, out_15}), .clk(multiplexer_5_out),
    .clr(multiplexer_6_out));
  _7_Segment u_7_segment_5 (
    .X3(out_15), .X2(out_16), .X1(out_17), .X0(out_18), .on(1'b1), .A(_1_2[0]), .B(_1_2[1]), .C(_1_2[2]),
    .D(_1_2[3]), .E(_1_2[4]), .F(_1_2[5]), .G(_1_2[6]), .dot(_1_2[7]));
endmodule
